# Fritzing sketch circuit diagram (saved by Fritzing 0.9.3b)
breadboards: 1

parts:
  Part1 = Arduino Nano (Rev3.0)
  PWM1 = PCA9685 16x12-bit PWM Breakout
  J2 = Basic Servo
  J3 = Basic Servo
  J4 = Basic Servo
  J5 = Basic Servo
  J6 = Basic Servo
  J7 = Basic Servo

nets:
  N1: Part1.D9, PWM1.no_name_yet#100, PWM1.no_name_yet#101, PWM1.no_name_yet#104, PWM1.no_name_yet#105, PWM1.no_name_yet#108, PWM1.no_name_yet#109, PWM1.no_name_yet#506
  N2: Part1.D11/MOSI, PWM1.no_name_yet#501, PWM1.no_name_yet#1000, PWM1.no_name_yet#1001, PWM1.no_name_yet#1004, PWM1.no_name_yet#1005, PWM1.no_name_yet#1008, PWM1.no_name_yet#1009
  N3: Part1.A6, J4.pulse
  N4: Part1.A5, J5.pulse
  N5: Part1.A4, J6.pulse
  N6: Part1.A3, J7.pulse
  N7: Part1.A2, J3.pulse
  N8: Part1.A1, J2.pulse
